# Fritzing sketch 8bitDAC (saved by Fritzing 0.8.7b)
breadboards: 1

parts:
  R13 = Resistor [tolerance=±5% resistance=20k package=THT]
  R20 = Resistor [tolerance=±5% resistance=10k package=THT]
  R15 = Resistor [tolerance=±5% resistance=20k package=THT]
  R26 = Resistor [tolerance=±5% resistance=10k package=THT]
  R24 = Resistor [tolerance=±5% resistance=10k package=THT]
  R27 = Rotary Potentiometer (Small)
  Bauteil1 = Arduino Uno (Rev3)
  R23 = Resistor [tolerance=±5% resistance=10k package=THT]
  R19 = Resistor [tolerance=±5% resistance=20k package=THT]
  R16 = Resistor [tolerance=±5% resistance=20k package=THT]
  R14 = Resistor [tolerance=±5% resistance=20k package=THT]
  R18 = Resistor [tolerance=±5% resistance=20k package=THT]
  R21 = Resistor [tolerance=±5% resistance=10k package=THT]
  R12 = Resistor [tolerance=±5% resistance=20k package=THT]
  R17 = Resistor [tolerance=±5% resistance=20k package=THT]
  R25 = Resistor [tolerance=±5% resistance=10k package=THT]
  R22 = Resistor [tolerance=±5% resistance=10k package=THT]
  J1 = Piezo Speaker
  R28 = Resistor [tolerance=±5% resistance=10k package=THT]

nets:
  N1: R13.Pin_0, R20.Pin_0, R23.Pin_1
  N2: R13.Pin_1, Bauteil1.D5_PWM
  N3: R20.Pin_1, R26.Pin_0, R14.Pin_0
  N4: R15.Pin_0, R26.Pin_1, R24.Pin_0
  N5: R15.Pin_1, Bauteil1.D3_PWM
  N6: R24.Pin_1, R16.Pin_0, R25.Pin_0
  N7: R27.leg1, Bauteil1.GND, J1.pin1, R28.Pin_0
  N8: R27.wiper, Bauteil1.A0
  N9: R27.leg2, Bauteil1.5V
  N10: Bauteil1.D0/RX, R19.Pin_1
  N11: Bauteil1.D1/TX, R18.Pin_1
  N12: Bauteil1.D2, R16.Pin_1
  N13: Bauteil1.D4, R14.Pin_1
  N14: Bauteil1.D6_PWM, R17.Pin_1
  N15: Bauteil1.D7, R12.Pin_1
  N16: R23.Pin_0, R21.Pin_1, R17.Pin_0
  N17: R19.Pin_0, R22.Pin_1, R28.Pin_1
  N18: R18.Pin_0, R25.Pin_1, R22.Pin_0
  N19: R21.Pin_0, R12.Pin_0, J1.pin2

custom parts:
  Rotary Potentiometer (Small): A rotary adjustable resistor (potentiometer).
