# Fritzing sketch ampelFertig (saved by Fritzing 0.9.1b)
breadboards: 1

parts:
  Bauteil1 = Arduino Uno (Rev3)
  R1 = Resistor [tolerance=±5% resistance=220 package=THT]
  R2 = Resistor [tolerance=±5% resistance=220 package=THT]
  R3 = Resistor [tolerance=±5% resistance=220 package=THT]
  R4 = Resistor [tolerance=±5% resistance=220 package=THT]
  R5 = Resistor [tolerance=±5% resistance=220 package=THT]
  S1 = Pushbutton [package="[THT]"]
  LED1 = LED - 5mm [color="Green (565nm)" package="5 mm [THT]"]
  R6 = Resistor [tolerance=±5% resistance=220 package=THT]
  R6_2 = Resistor [tolerance=±5% resistance=10k package=THT]
  LED5 = LED - 5mm [color="Red (633nm)" package="5 mm [THT]"]
  LED4 = LED - 5mm [color="Yellow (585nm)" package="5 mm [THT]"]
  LED3 = LED - 5mm [color="Green (555nm)" package="5 mm [THT]"]
  LED2 = LED - 5mm [color="Red (633nm)" package="5 mm [THT]"]

nets:
  N1: Bauteil1.D8, LED5.anode
  N2: Bauteil1.D9_PWM, LED4.anode
  N3: Bauteil1.D10_PWM/SS, LED3.anode
  N4: Bauteil1.D12/MISO, LED2.anode
  N5: Bauteil1.D13/SCK, LED1.anode
  N6: Bauteil1.D2, S1.Pin_1, S1.Pin_2, R6.Pin_1, R6_2.Pin_1
  N7: Bauteil1.5V, S1.Pin_3, S1.Pin_4
  N8: Bauteil1.GND, R1.Pin_0, R2.Pin_0, R3.Pin_0, R4.Pin_0, R5.Pin_0, R6.Pin_0, R6_2.Pin_0
  N9: R1.Pin_1, LED1.cathode
  N10: R2.Pin_1, LED2.cathode
  N11: R3.Pin_1, LED3.cathode
  N12: R4.Pin_1, LED4.cathode
  N13: R5.Pin_1, LED5.cathode
