# Fritzing sketch ampelG (saved by Fritzing 0.9.1b)
breadboards: 1

parts:
  Bauteil1 = Arduino Uno (Rev3)
  R3 = Resistor [tolerance=±5% resistance=220 package=THT]
  LED3 = LED - 5mm [color="Green (555nm)" package="5 mm [THT]"]

nets:
  N1: Bauteil1.D10_PWM/SS, LED3.anode
  N2: Bauteil1.GND, R3.Pin_0
  N3: R3.Pin_1, LED3.cathode
