# Fritzing sketch digitalA0 (saved by Fritzing 0.9.0b)
breadboards: 1

parts:
  Bauteil1 = Arduino Uno (Rev3)
  R1 = Resistor [tolerance=±5% resistance=220 package=THT]
  LED1 = LED - 5mm [color="Red (633nm)" package="5 mm [THT]"]

nets:
  N1: Bauteil1.A0, R1.Pin_0
  N2: Bauteil1.GND, LED1.cathode
  N3: R1.Pin_1, LED1.anode
