# Fritzing sketch digitalreadserial2-led (saved by Fritzing 0.9.1b)
breadboards: 1

parts:
  Bauteil1 = Arduino Uno (Rev3)
  S1 = Pushbutton [package="[THT]"]
  R1 = Resistor [tolerance=±5% resistance=10k package=THT]
  LED1 = LED - 5mm [color="Red (633nm)" package="5 mm [THT]"]

nets:
  N1: Bauteil1.D13/SCK, LED1.anode
  N2: Bauteil1.GND, R1.Pin_0, LED1.cathode
  N3: Bauteil1.D2, S1.Pin_1, S1.Pin_2, R1.Pin_1
  N4: Bauteil1.5V, S1.Pin_3, S1.Pin_4
