# Fritzing sketch pull-resistors (saved by Fritzing 0.8.7b)
breadboards: 1

parts:
  Arduino2 = Arduino Uno (Rev3) - ICSP
  R1 = Resistor [tolerance=±5% resistance=10k package=THT]
  R2 = Resistor [tolerance=±5% resistance=10k package=THT]

nets:
  N1: Arduino2.D3_PWM, R1.Pin_1
  N2: Arduino2.D5_PWM, R2.Pin_1
  N3: Arduino2.5V, R2.Pin_0
  N4: Arduino2.GND, R1.Pin_0
