# Fritzing sketch cny70 (saved by Fritzing 0.8.7b)
breadboards: 1

parts:
  Bauteil1 = Arduino Uno (Rev3)
  R1 = Resistor [tolerance=±5% resistance=220 package=THT]
  R2 = Resistor [tolerance=±5% resistance=10k package=THT]
  CNY3 = CNY70  # not connected

nets:
  N1: Bauteil1.A0, R2.Pin_0
  N2: Bauteil1.5V, R1.Pin_1, R2.Pin_1

custom parts:
  CNY70: Sensor de Infrarojos de corto alcance.
