# Fritzing sketch cny70bb (saved by Fritzing 0.9.2b)
breadboards: 1

parts:
  Bauteil1 = Arduino Uno (Rev3)
  R1 = Resistor [tolerance=±5% resistance=220 package=THT]
  R2 = Resistor [tolerance=±5% resistance=10k package=THT]

nets:
  N1: Bauteil1.A0, R2.Pin_1
  N2: Bauteil1.5V, R1.Pin_1, R2.Pin_0
