# Fritzing sketch delay_mills (saved by Fritzing 0.8.7b)
breadboards: 1

parts:
  Bauteil1 = Arduino Uno (Rev3)
  S1 = Pushbutton [package="[THT]"]
  R1 = Resistor [tolerance=±5% resistance=10k package=THT]
  R2 = Resistor [tolerance=±5% resistance=220 package=THT]
  LED1 = LED - 5mm [color="Red (633nm)" package="5 mm [THT]"]
  LED2 = LED - 5mm [color="Green (565nm)" package="5 mm [THT]"]
  R3 = Resistor [tolerance=±5% resistance=220 package=THT]

nets:
  N1: Bauteil1.D11_PWM/MOSI, LED2.anode
  N2: Bauteil1.D13/SCK, LED1.anode
  N3: Bauteil1.GND, R1.Pin_0, R2.Pin_1, R3.Pin_1
  N4: Bauteil1.D2, S1.Pin_3, S1.Pin_4, R1.Pin_1
  N5: Bauteil1.5V, S1.Pin_1, S1.Pin_2
  N6: R2.Pin_0, LED1.cathode
  N7: LED2.cathode, R3.Pin_0
