# Fritzing sketch ifelse (saved by Fritzing 0.8.7b)
breadboards: 1

parts:
  Bauteil1 = Arduino Uno (Rev3)
  S1 = Pushbutton [package="[THT]"]
  R1 = Resistor [tolerance=±5% resistance=10k package=THT]
  T1 = LM35 Temperature Sensor [package="TO92 [THT]"]
  LED1 = RGB LED (com. anode, rbg) [package="5 mm [THT]"]
  R2 = Resistor [tolerance=±5% resistance=470 package=THT]
  R3 = Resistor [tolerance=±5% resistance=470 package=THT]
  R4 = Resistor [tolerance=±5% resistance=470 package=THT]

nets:
  N1: Bauteil1.A5/SCL, T1.Vout
  N2: Bauteil1.D11_PWM/MOSI, R4.Pin_0
  N3: Bauteil1.D12/MISO, R3.Pin_0
  N4: Bauteil1.D13/SCK, R2.Pin_0
  GND: Bauteil1.GND, R1.Pin_0, T1.GND, LED1.common_anode
  N5: Bauteil1.D2, S1.Pin_3, S1.Pin_4, R1.Pin_1
  N6: Bauteil1.5V, S1.Pin_1, S1.Pin_2, T1.+Vs
  N7: LED1.red_cathode, R4.Pin_1
  N8: LED1.blue_cathode, R3.Pin_1
  N9: LED1.green_cathode, R2.Pin_1
