# Fritzing sketch ldr_bb (saved by Fritzing 0.9.2b)
breadboards: 1

parts:
  Bauteil1 = Arduino Uno (Rev3)
  R6 = Resistor [tolerance=±5% resistance=10k package=THT]
  R6_2 = Resistor [tolerance=±5% resistance=10k package=THT]
  R7 = Photocell (LDR) [package=THT]

nets:
  N1: Bauteil1.A0, R6.Pin_1, R6_2.Pin_1, R7.pin_0
  N2: Bauteil1.5V, R7.pin_1
  N3: Bauteil1.GND, R6.Pin_0, R6_2.Pin_0
