# Fritzing sketch parkhilfe (saved by Fritzing 0.8.7b)
breadboards: 1

parts:
  Bauteil1 = Arduino Uno (Rev3)
  UDS1 = PING Ultrasonic Sensor
  UDS2 = PING Ultrasonic Sensor
  LED1 = LED - 5mm [color="Red (633nm)" package="5 mm [THT]"]
  LED2 = LED - 5mm [color="Red (633nm)" package="5 mm [THT]"]
  LED3 = LED - 5mm [color="Orange (612nm)" package="5 mm [THT]"]
  LED4 = LED - 5mm [color="Orange (612nm)" package="5 mm [THT]"]
  LED5 = LED - 5mm [color="Yellow (592nm)" package="5 mm [THT]"]
  LED6 = LED - 5mm [color="Yellow (592nm)" package="5 mm [THT]"]
  LED7 = LED - 5mm [color="Green (565nm)" package="5 mm [THT]"]
  LED8 = LED - 5mm [color="Green (565nm)" package="5 mm [THT]"]
  LED9 = LED - 5mm [color="Green (565nm)" package="5 mm [THT]"]
  R1 = Resistor [tolerance=±5% resistance=220 package=THT]
  R2 = Resistor [tolerance=±5% resistance=220 package=THT]
  R3 = Resistor [tolerance=±5% resistance=220 package=THT]
  R4 = Resistor [tolerance=±5% resistance=220 package=THT]
  R5 = Resistor [tolerance=±5% resistance=220 package=THT]
  R6 = Resistor [tolerance=±5% resistance=220 package=THT]
  R7 = Resistor [tolerance=±5% resistance=220 package=THT]
  R8 = Resistor [tolerance=±5% resistance=220 package=THT]
  R9 = Resistor [tolerance=±5% resistance=220 package=THT]
  Bauteil2 = Shift Register Breakout - 74HC595  # not connected

nets:
  N1: Bauteil1.D8, LED7.anode
  N2: Bauteil1.D9_PWM, LED5.anode
  N3: Bauteil1.D10_PWM/SS, LED3.anode
  N4: Bauteil1.D11_PWM/MOSI, LED1.anode
  N5: Bauteil1.D13/SCK, UDS1.I/O
  GND: Bauteil1.GND, UDS1.GND, UDS2.GND, R1.Pin_0, R2.Pin_0, R3.Pin_0, R4.Pin_0, R5.Pin_0, R6.Pin_0, R7.Pin_0, R8.Pin_0, R9.Pin_0
  N6: Bauteil1.D2, UDS2.I/O
  N7: Bauteil1.D3_PWM, LED2.anode
  N8: Bauteil1.D4, LED4.anode
  N9: Bauteil1.D5_PWM, LED6.anode
  N10: Bauteil1.D6_PWM, LED8.anode
  N11: Bauteil1.D7, LED9.anode
  VCC: Bauteil1.5V, UDS1.VCC, UDS2.VCC
  N12: LED1.cathode, R1.Pin_1
  N13: LED2.cathode, R9.Pin_1
  N14: LED3.cathode, R2.Pin_1
  N15: LED4.cathode, R8.Pin_1
  N16: LED5.cathode, R3.Pin_1
  N17: LED6.cathode, R7.Pin_1
  N18: LED7.cathode, R4.Pin_1
  N19: LED8.cathode, R6.Pin_1
  N20: LED9.cathode, R5.Pin_1

custom parts:
  PING Ultrasonic Sensor: The PING)))™ ultrasonic sensor provides an easy method of distance measurement. This sensor is perfect for any number of applications that require you to perform measurements between moving or stationary objects. Interfacing to a microcontroller is a snap. A single I/O pin is used to trigger an ultrasonic burst (well above human hearing) and then "listen" for the echo return pulse. The sensor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
