# Fritzing sketch ping))) (saved by Fritzing 0.9.2b)
breadboards: 1

parts:
  Bauteil1 = Arduino Uno (Rev3)
  UDS1 = PING Ultrasonic Sensor

nets:
  N1: Bauteil1.D2, UDS1.I/O
  5V: Bauteil1.5V, UDS1.VCC
  GND: Bauteil1.GND, UDS1.GND

custom parts:
  PING Ultrasonic Sensor: The PING)))™ ultrasonic sensor provides an easy method of distance measurement. This sensor is perfect for any number of applications that require you to perform measurements between moving or stationary objects. Interfacing to a microcontroller is a snap. A single I/O pin is used to trigger an ultrasonic burst (well above human hearing) and then "listen" for the echo return pulse. The sensor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
