# Fritzing sketch ping_bb (saved by Fritzing 0.9.2b)
breadboards: 1

parts:
  Bauteil1 = Arduino Uno (Rev3)
  R3 = Resistor [tolerance=±5% resistance=220 package=THT]
  R4 = Resistor [tolerance=±5% resistance=220 package=THT]
  R5 = Resistor [tolerance=±5% resistance=220 package=THT]
  LED5 = LED - 5mm [color="Red (633nm)" package="5 mm [THT]"]
  LED4 = LED - 5mm [color="Yellow (585nm)" package="5 mm [THT]"]
  LED3 = LED - 5mm [color="Green (555nm)" package="5 mm [THT]"]
  Bauteil2 = SRF05 Ultrasonic Rangefinder

nets:
  N1: Bauteil1.D8, LED5.anode
  N2: Bauteil1.D9_PWM, LED4.anode
  N3: Bauteil1.D10_PWM/SS, LED3.anode
  N4: Bauteil1.D2, Bauteil2.Echo
  N5: Bauteil1.D3_PWM, Bauteil2.Trig
  5V: Bauteil1.5V, Bauteil2.VCC
  GND: Bauteil1.GND, R3.Pin_0, R4.Pin_0, R5.Pin_0, Bauteil2.GND
  N6: R3.Pin_1, LED3.cathode
  N7: R4.Pin_1, LED4.cathode
  N8: R5.Pin_1, LED5.cathode
