# Fritzing sketch potentiometer (saved by Fritzing 0.9.2b)
breadboards: 1

parts:
  Bauteil1 = Arduino Uno (Rev3)
  R3 = Resistor [tolerance=±5% resistance=220 package=THT]
  R4 = Resistor [tolerance=±5% resistance=220 package=THT]
  R5 = Resistor [tolerance=±5% resistance=220 package=THT]
  LED5 = LED - 5mm [color="Red (633nm)" package="5 mm [THT]"]
  LED4 = LED - 5mm [color="Yellow (585nm)" package="5 mm [THT]"]
  LED3 = LED - 5mm [color="Green (555nm)" package="5 mm [THT]"]
  R6 = Rotary Potentiometer (Small) [maximum_resistance=100kΩ package=THT]

nets:
  N1: Bauteil1.A0, R6.wiper
  N2: Bauteil1.D8, LED5.anode
  N3: Bauteil1.D9_PWM, LED4.anode
  N4: Bauteil1.D10_PWM/SS, LED3.anode
  N5: Bauteil1.5V, R6.leg2
  N6: Bauteil1.GND, R3.Pin_0, R4.Pin_0, R5.Pin_0, R6.leg1
  N7: R3.Pin_1, LED3.cathode
  N8: R4.Pin_1, LED4.cathode
  N9: R5.Pin_1, LED5.cathode
