# Fritzing sketch temperatursensor (saved by Fritzing 0.9.1b)
breadboards: 1

parts:
  T1 = LM35 Temperature Sensor [package="TO92 [THT]"]
  Bauteil2 = Arduino Uno (Rev3)
  R6 = Resistor [tolerance=±5% resistance=220 package=THT]
  R7 = Resistor [tolerance=±5% resistance=220 package=THT]
  R8 = Resistor [tolerance=±5% resistance=220 package=THT]
  LED6 = LED - 5mm [color="Green (555nm)" package="5 mm [THT]"]
  LED7 = LED - 5mm [color="Yellow (585nm)" package="5 mm [THT]"]
  LED8 = LED - 5mm [color="Red (633nm)" package="5 mm [THT]"]

nets:
  N1: T1.+Vs, Bauteil2.5V
  N2: T1.Vout, Bauteil2.A0
  GND: T1.GND, Bauteil2.GND, R6.Pin_0, R7.Pin_0, R8.Pin_0
  N3: Bauteil2.D8, LED8.anode
  N4: Bauteil2.D9_PWM, LED7.anode
  N5: Bauteil2.D10_PWM/SS, LED6.anode
  N6: R6.Pin_1, LED8.cathode
  N7: R7.Pin_1, LED7.cathode
  N8: R8.Pin_1, LED6.cathode
