# Fritzing sketch L293D_breadboard (saved by Fritzing 0.9.2b)
breadboards: 1

parts:
  Bauteil1 = Arduino Uno (Rev3)
  IC1 = L293D [package=THT]
  M1 = DC Motor

nets:
  N1: Bauteil1.D9_PWM, IC1.In_3
  N2: Bauteil1.D10_PWM/SS, IC1.In_4
  N3: Bauteil1.GND, IC1.0V
  N4: Bauteil1.D5_PWM, IC1.In_1
  N5: Bauteil1.D6_PWM, IC1.In_2
  N6: Bauteil1.5V, IC1.Enable_1, IC1.Enable_2, IC1.+V
  N7: Bauteil1.VIN, IC1.+Vmotor
  N8: IC1.Out_1_(_Controlled_by_Enable_1_), M1.pin_1
  N9: IC1.Out_2_(_Controlled_by_Enable_1_), M1.pin_2
