# Fritzing sketch LCD (saved by Fritzing 0.9.0b)
breadboards: 1

parts:
  Arduino1 = Arduino Uno (Rev3)
  U1 = LCD-16X2 [package=lcd-16x2]
  R1 = Trimmer Potentiometer [maximum_resistance=100kΩ package=THT]
  S1 = Pushbutton [package="[THT]"]
  S2 = Pushbutton [package="[THT]"]
  S3 = Pushbutton [package="[THT]"]
  R2 = Resistor [tolerance=±5% resistance=10k package=THT]
  R3 = Resistor [tolerance=±5% resistance=10k package=THT]
  R4 = Resistor [tolerance=±5% resistance=10k package=THT]

nets:
  N1: Arduino1.D8, S1.Pin_3, S1.Pin_4, R4.Pin_1
  N2: Arduino1.D9_PWM, S2.Pin_3, S2.Pin_4, R2.Pin_1
  N3: Arduino1.D10_PWM/SS, S3.Pin_3, S3.Pin_4, R3.Pin_1
  N4: Arduino1.D11_PWM/MOSI, U1.E
  N5: Arduino1.D12/MISO, U1.RS
  GND: Arduino1.GND, U1.VSS, U1.R_W, R1.leg1, R1.leg2, S1.Pin_1, S1.Pin_2, S2.Pin_1, S2.Pin_2, S3.Pin_1, S3.Pin_2, R2.Pin_0, R3.Pin_0, R4.Pin_0
  N6: Arduino1.D2, U1.DB4
  N7: Arduino1.D3_PWM, U1.DB5
  N8: Arduino1.D4, U1.DB6
  N9: Arduino1.D5_PWM, U1.DB7
  5V: Arduino1.5V, U1.VDD
  N10: U1.VO, R1.wiper
