# Fritzing sketch ServoSchaltung (saved by Fritzing 0.9.2b)
breadboards: 1

parts:
  J1 = Basic Servo
  Arduino1 = Arduino Uno (Rev3)

nets:
  GND: J1.gnd, Arduino1.GND
  VCC: J1.vcc, Arduino1.5V
  N1: J1.pulse, Arduino1.D3_PWM
