# Fritzing sketch nema17A4988 (saved by Fritzing 0.9.2b)
breadboards: 1

parts:
  Part1 = Arduino Uno (Rev3)
  MD09B1 = A4988 Stepper Motor Driver Carrier
  M1 = Stepper Motor - Bipolar
  C2 = Electrolytic Capacitor [capacitance=100nF voltage=16V package="100 mil [THT, electrolytic]"]

nets:
  N1: Part1.D8, MD09B1.STEP
  N2: Part1.D9_PWM, MD09B1.DIR
  N3: Part1.D3_PWM, MD09B1.Enable
  N4: Part1.D4, MD09B1.MS1
  N5: Part1.D5_PWM, MD09B1.MS2
  N6: Part1.D6_PWM, MD09B1.MS3
  5V: Part1.5V, MD09B1.VDD
  N7: Part1.GND, MD09B1.GROUND#147
  N8: MD09B1.RESET, MD09B1.SLEEP
  N9: MD09B1.VMOT, C2.+
  N10: MD09B1.GROUND#141, C2.-
  N11: MD09B1.OUT_2B, M1.D
  N12: MD09B1.OUT_2A, M1.C
  N13: MD09B1.OUT_1A, M1.B
  N14: MD09B1.OUT_1B, M1.A

notes:
  12V Power Supply
