# Fritzing sketch npn-Verstärker (saved by Fritzing 0.8.7b)
breadboards: 1

parts:
  Bauteil1 = Arduino Uno (Rev3)
  Q1 = NPN-Transistor [package="TO92 [THT]"]
  R1 = Resistor [tolerance=±5% resistance=100 package=THT]
  R2 = Rotary Potentiometer (Small) [maximum_resistance=10kΩ package=THT]
  J1 = Piezo Speaker

nets:
  N1: Bauteil1.D9_PWM, R2.wiper
  N2: Bauteil1.5V, J1.pin2
  N3: Bauteil1.GND, Q1.E
  N4: Q1.B, R1.Pin_0
  N5: Q1.C, J1.pin1
  N6: R1.Pin_1, R2.leg2
