# Fritzing sketch peltier (saved by Fritzing 0.9.2b)
breadboards: 1

parts:
  Arduino1 = Arduino Uno (Rev3)
  VCC1 = Battery block 9V  # not connected
  J3 = Peltier Element
  Q2 = Basic FET N-Channel [package="TO220 [THT]"]
  R2 = Resistor [tolerance=±5% resistance=1k package=THT]

nets:
  N1: Arduino1.D3_PWM, Q2.gate
  N2: Arduino1.GND, Q2.source, R2.Pin_1
  N3: J3.pin1, Q2.drain

notes:
  BLINK

// code stored in the sketch: Blink.ino
/*
  Blink
  
  Schaltet eine LED im Rythmus von einer Sekunde an und aus
  
  Dieses Beispiel aus dem Fritzing Creator Kit: www.fritzing.org/creator-kit.
*/

int led = 13;                   // ganzzahlige Variable led wird deklariert

void setup() {                  // die setup()-Methode wird einmal ausgeführt
  pinMode(led, OUTPUT);     
}

void loop() {                   // die loop()-Methode wird immer wiederholt
  digitalWrite(led, HIGH);      // schaltet die LED ein 
  delay(1000);                  // hält das Programm für 1000 Millisekunden an
  digitalWrite(led, LOW);       // schaltet die LED ab
  delay(1000);                  // hält das Programm für 1000 Millisekunden an
}
