# Fritzing sketch rgb-mischer (saved by Fritzing 0.8.7b)
circuit board: 6.88566cm x 5.36311cm
circuit board: 6.88566cm x 5.36311cm
breadboards: 1

parts:
  R5 = Resistor [tolerance=±5% resistance=220 package=THT]
  R6 = Resistor [tolerance=±5% resistance=220 package=THT]
  R7 = Resistor [tolerance=±5% resistance=220 package=THT]
  LED2 = RGB LED (com. cathode, rbg) [package="5 mm [THT]"]
  R8 = Rotary Potentiometer (Small) [maximum_resistance=100kΩ package=THT]
  Arduino2 = Arduino Uno (Rev3)
  R9 = Rotary Potentiometer (Small) [maximum_resistance=100kΩ package=THT]
  R10 = Rotary Potentiometer (Small) [maximum_resistance=100kΩ package=THT]

nets:
  N1: R5.Pin_0, LED2.red_anode
  N2: R5.Pin_1, Arduino2.D11_PWM/MOSI
  N3: R6.Pin_0, LED2.blue_anode
  N4: R6.Pin_1, Arduino2.D10_PWM/SS
  N5: R7.Pin_0, LED2.green_anode
  N6: R7.Pin_1, Arduino2.D9_PWM
  N7: LED2.common_cathode, R8.leg1, Arduino2.GND, R9.leg1, R10.leg1
  N8: R8.wiper, Arduino2.A0
  N9: R8.leg2, Arduino2.5V, R9.leg2, R10.leg2
  N10: Arduino2.A1, R9.wiper
  N11: Arduino2.A2, R10.wiper

notes:
  This is the same example, but using a "common cathode" RGB LED.
  Note that its long pin connects to - instead of +.
  This example is using the type in the Fritzing Starter Kits (pins: blue, common cathode, red, green).

// code stored in the sketch: color-fader.ino
/*
  _____       .__  __         .__                
_/ ____\______|__|/  |________|__| ____    ____  
\   __\\_  __ \  \   __\___   /  |/    \  / ___\ 
 |  |   |  | \/  ||  |  /    /|  |   |  \/ /_/  >
 |__|   |__|  |__||__| /_____ \__|___|  /\___  / 
                             \/       \//_____/  
          __                 __                  __   .__  __   
  _______/  |______ ________/  |_  ___________  |  | _|__|/  |_ 
 /  ___/\   __\__  \\_  __ \   __\/ __ \_  __ \ |  |/ /  \   __\
 \___ \  |  |  / __ \|  | \/|  | \  ___/|  | \/ |    <|  ||  |  
/____  > |__| (____  /__|   |__|  \___  >__|    |__|_ \__||__|  
     \/            \/                 \/             \/         

Example      RGB LED Fader
Autor        Stefan Hermann
Date         16.06.2011

Description  This example lets you fade through the colors of a RGB LED.

NOTE         This example expects an RGB LED of the type "common anode".
             If your type is "common cathode", the brightness will be reversed.

*/

int LEDGreen=9;
int LEDBlue=10;
int LEDRed=11;


int sensorPin=0;
int val;

void setup(){
  Serial.begin(9600);
  pinMode(LEDRed,OUTPUT);
  pinMode(LEDGreen,OUTPUT);
  pinMode(LEDBlue,OUTPUT);  
}

void loop(){
  
  val=map(analogRead(sensorPin),0,1024,0,900);
  Serial.println(val);
  if (val<150) {
    analogWrite(LEDRed,0);
    analogWrite(LEDBlue,255); 
    analogWrite(LEDGreen,255);    
  } else if (val<300) {
    analogWrite(LEDRed,map(val,150,300,0,255));
    analogWrite(LEDBlue,map(val,150,300,255,0)); 
    analogWrite(LEDGreen,255);
  } else if (val<450) {
    analogWrite(LEDRed,255);
    analogWrite(LEDBlue,0); 
    analogWrite(LEDGreen,255);  
  } else if (val<600) {
    analogWrite(LEDRed,255);
    analogWrite(LEDBlue,map(val,450,600,0,255)); 
    analogWrite(LEDGreen,map(val,450,600,255,0));
  } else if (val<750) {
    analogWrite(LEDRed,255);
    analogWrite(LEDBlue,255); 
    analogWrite(LEDGreen,0);  
  } else if (val<900) {
    analogWrite(LEDRed,map(val,750,900,255,0));
    analogWrite(LEDBlue,255); 
    analogWrite(LEDGreen,map(val,750,900,0,255));
  }
  delay(10);
}
