# Fritzing sketch rgb (saved by Fritzing 0.9.2b)
breadboards: 1

parts:
  Arduino1 = Arduino Uno (Rev3)
  LED1 = RGB LED (com. cathode, rgb) [package="5 mm [THT]"]
  R7 = Resistor [resistance=220 tolerance=±5% package=THT]
  R8 = Resistor [resistance=220 tolerance=±5% package=THT]
  R9 = Resistor [resistance=220 tolerance=±5% package=THT]

nets:
  N1: Arduino1.D11_PWM/MOSI, R9.Pin_0
  N2: Arduino1.D12/MISO, R7.Pin_0
  N3: Arduino1.D13/SCK, R8.Pin_0
  N4: Arduino1.GND, LED1.common_cathode
  N5: LED1.red_anode, R9.Pin_1
  N6: LED1.green_anode, R7.Pin_1
  N7: LED1.blue_anode, R8.Pin_1

notes:
  Let the light shine in any color!
  Check out this forum post for a good code example.
