# Fritzing sketch ton-nfet (saved by Fritzing 0.9.2b)
breadboards: 1

parts:
  Bauteil1 = Arduino Uno (Rev3)
  Q2 = Basic FET N-Channel [package="D2Pak [SMD]"]
  J1 = Piezo Speaker

nets:
  N1: Bauteil1.D3_PWM, Q2.Gate
  N2: Bauteil1.5V, J1.pin2
  N3: Bauteil1.GND, Q2.source
  N4: Q2.drain, J1.pin1
