# Fritzing sketch ton-npn (saved by Fritzing 0.9.2b)
breadboards: 1

parts:
  Bauteil1 = Arduino Uno (Rev3)
  R2 = Rotary Potentiometer (Small) [maximum_resistance=100kΩ package=THT]
  Q1 = NPN-Transistor [package="TO92 [THT]"]
  J1 = Piezo Speaker
  R3 = Resistor [tolerance=±5% resistance=100 package=THT]

nets:
  N1: Bauteil1.D3_PWM, R2.leg1
  N2: Bauteil1.5V, J1.pin2
  N3: Bauteil1.GND, Q1.E
  N4: R2.wiper, R3.Pin_1
  N5: Q1.B, R3.Pin_0
  N6: Q1.C, J1.pin1
