# Fritzing sketch ton-poti (saved by Fritzing 0.9.2b)
breadboards: 1

parts:
  Bauteil1 = Arduino Uno (Rev3)
  J2 = Piezo Speaker
  R2 = Rotary Potentiometer (Small) [maximum_resistance=100kΩ package=THT]

nets:
  N1: Bauteil1.D3_PWM, R2.leg1
  N2: Bauteil1.GND, J2.pin1
  N3: J2.pin2, R2.wiper
